// Logisim project CPU Project.circ as structural Verilog
module ALU_SHIFTER (
  input  [31:0] B__32,
  input  [4:0] Sa__5,
  input  [3:0] Op__4,
  output [31:0] C__32
);

  wire bitselector_1_out, bitselector_2_out;

  BitSelector #(.width(4)) bitselector_1 (.in(Op__4), .out(bitselector_1_out), .sel(2'b00));
  BitSelector #(.width(4)) bitselector_2 (.in(Op__4), .out(bitselector_2_out), .sel(2'b10));
  _32_BIT_SHIFTER u_32_bit_shifter_1 (
    .Input__32(B__32), .Sa__5(Sa__5), .Cin(bitselector_1_out), .Direction__1(bitselector_2_out), .out_5(C__32));
endmodule

module ALU (
  input  [31:0] A__32,
  input  [31:0] B__32,
  input  [4:0] Sa__5,
  input  [3:0] Op__4
);

  wire bitselector_1_out, bitselector_2_out;
  wire [31:0] alu_shifter_1_c__32, transistor_2_out;

  Transistor #(.gate("br"), .width(32)) transistor_1 (.in(B__32), .gate(bitselector_1_out));  // open: out
  Transistor #(.gate("br"), .width(32)) transistor_2 (.in(B__32), .out(transistor_2_out), .gate(bitselector_1_out));
  // NOT_Gate not_1 has open pins: in=bitselector_1_out, out=open
  BitSelector #(.width(4)) bitselector_1 (.in(Op__4), .out(bitselector_1_out), .sel(2'b11));
  BitSelector #(.width(4)) bitselector_2 (.in(Op__4), .out(bitselector_2_out), .sel(2'b01));
  ALU_SHIFTER alu_shifter_1 (.B__32(transistor_2_out), .Sa__5(Sa__5), .Op__4(Op__4), .C__32(alu_shifter_1_c__32));
  Multiplexer #(.width(32), .enable("false")) multiplexer_1 (
    .in1(alu_shifter_1_c__32), .sel(bitselector_2_out));  // open: in0, out
endmodule
