// Logisim project CPU.circ as structural Verilog: 1 circuit, main circuit CPU
module CPU (
  input  Immediate,
  input  Clock,
  output [31:0] Result
);

  wire Execute_p9, MEM_WB_load_store_2, Memory_p11, not_1_out, not_2_out, not_4_out, not_5_out;
  wire [3:0] Decode_opcode, Execute_p15, ID_EX_opcode_2;
  wire [4:0] Decode_rd, Decode_rt, Decode_shift, Execute_p16, Execute_p17, Fetch_clock_2, ID_EX_clock_data_2,
       ID_EX_rd_2, ID_EX_rt_2, ID_EX_shift_2, IF_ID_clock_data_2;
  wire [15:0] Decode_immediate, ID_EX_immediate_2;
  wire [31:0] Decode_a, Decode_b, EX_MEM_b_2, EX_MEM_d_2, Execute_p11, Execute_p12, Execute_p13, Execute_p14,
       Fetch_instructions, ID_EX_a_2, ID_EX_b_2, IF_ID_instructions_data_2, MEM_WB_d_2, MEM_WB_m_2,
       Memory_p9, Memory_p10, undriven;

  Fetch Fetch (.Clock(not_1_out), .Instructions(Fetch_instructions), .Clock_2(Fetch_clock_2));
  not not_1 (not_1_out, Clock);
  Decode Decode (
    .D(undriven), .Instruction(IF_ID_instructions_data_2), .Clock(not_2_out), .OpCode(Decode_opcode),
    .Shift(Decode_shift), .A(Decode_a), .B(Decode_b), .Immediate(Decode_immediate), .RT(Decode_rt),
    .RD(Decode_rd));
  IF_ID IF_ID (
    .Instructions_Data(Fetch_instructions), .Clock_Data(Fetch_clock_2), .Clock(Clock),
    .Instructions_Data_2(IF_ID_instructions_data_2), .Clock_Data_2(IF_ID_clock_data_2));
  not not_2 (not_2_out, Clock);
  ID_EX ID_EX (
    .OpCode(Decode_opcode), .Shift(Decode_shift), .A(Decode_a), .B(Decode_b), .Immediate(Decode_immediate),
    .RT(Decode_rt), .RD(Decode_rd), .Clock_Data(IF_ID_clock_data_2), .Clock(Clock),
    .OpCode_2(ID_EX_opcode_2), .Shift_2(ID_EX_shift_2), .A_2(ID_EX_a_2), .B_2(ID_EX_b_2),
    .Immediate_2(ID_EX_immediate_2), .RT_2(ID_EX_rt_2), .RD_2(ID_EX_rd_2), .Clock_Data_2(ID_EX_clock_data_2));
  // Execute Execute: pin names not known; wires that end beside it: ID_EX_opcode_2, ID_EX_shift_2, ID_EX_a_2, ID_EX_b_2, ID_EX_immediate_2, ID_EX_rt_2, ID_EX_rd_2, ID_EX_clock_data_2, Execute_p9, Immediate, Execute_p11, Execute_p12, Execute_p13, Execute_p14, Execute_p15, Execute_p16, Execute_p17
  not not_3 (Execute_p9, Clock);
  EX_MEM EX_MEM (
    .A(Execute_p11), .D(Execute_p12), .B(Execute_p13), .Target(Execute_p14), .OpCode(Execute_p15),
    .RT(Execute_p16), .RD(Execute_p17), .Clock(Clock), .D_2(EX_MEM_d_2), .B_2(EX_MEM_b_2));  // open: A_2, Target_2, OpCode_2, RT_2, RD_2
  not not_4 (not_4_out, Clock);
  // MEMORY_MODULE_main Memory: pin names not known; wires that end beside it: Execute_p13, Execute_p14, Execute_p15, Execute_p16, Execute_p17, EX_MEM_d_2, EX_MEM_b_2, not_4_out, Memory_p9, Memory_p10, Memory_p11
  MEM_WB_main MEM_WB (
    .D(Memory_p9), .M(Memory_p10), .Load_Store(Memory_p11), .Clock(Clock), .D_2(MEM_WB_d_2),
    .M_2(MEM_WB_m_2), .Load_Store_2(MEM_WB_load_store_2));  // open: OpCode, RT, RD, OpCode_2, RT_2, RD_2
  not not_5 (not_5_out, Clock);
  // WRITEBACK_MODULE_main Writeback: pin names not known; wires that end beside it: not_5_out, MEM_WB_d_2, MEM_WB_load_store_2, MEM_WB_m_2, Result
endmodule
