// Logisim project Control32.circ as structural Verilog: 1 circuit, main circuit main
module main (
  input  [31:0] in_1,
  output W,
  output [4:0] Rw,
  output [4:0] Ra,
  output [4:0] Rb,
  output [3:0] Op
);
endmodule
