// Logisim project FETCH MODULE.circ as structural Verilog: 2 circuits, main circuit Fetch
module Fetch (
  input  Clock,
  output [31:0] Instructions,
  output [4:0] Clock_2
);

  Clock clock_1 (.Clock(Clock), .out_2(Clock_2));
  ROM #(.addrWidth(5), .dataWidth(32)) rom_1 (.addr(Clock_2), .data(Instructions));  // open: sel

  // Notes on the sheet:
  //   contents of rom_1 (hex, n*v repeats v):
  //   27180005 25290003 138c023
endmodule

module Clock (
  input  Clock,
  output [4:0] out_2
);

  wire [4:0] adder_1_out;

  Adder #(.width(5)) adder_1 (.a(out_2), .b(5'b00001), .out(adder_1_out));  // open: cin, cout
  Register #(.width(5)) register_1 (.D(adder_1_out), .Q(out_2), .clk(Clock));  // open: en, clr
endmodule
