// Logisim project Subtract32.circ as structural Verilog: 1 circuit, main circuit main
module main (
  input  [31:0] A,
  input  [31:0] in_2,
  input  [3:0] in_3,
  input  [1:0] in_4,
  output [31:0] out_5,
  output Overflow
);

  wire bitselector_1_out, main_1_overflow;
  wire [31:0] not_1_out;

  assign not_1_out = ~in_2;  // NOT_Gate not_1, 32 bits wide
  BitSelector #(.width(4)) bitselector_1 (.in(in_3), .out(bitselector_1_out), .sel(in_4));
  Add32_main main_1 (.A(A), .B(not_1_out), .Out(out_5), .in_3(1'b1), .Overflow(main_1_overflow));
  xor xor_1 (Overflow, main_1_overflow, 1'b1);

  // Notes on the sheet:
  //   B
  //   Out (32)
endmodule
